# Fritzing sketch jetson_finder_schmetics (saved by Fritzing 0.9.4)
breadboards: 2

parts:
  Jetson_Nano2 = Jetson Nano
  R1 = Resistor [tolerance=±5% resistance=220 package=THT]
  S1 = Momentary Switch [package=ksa_sealed_tac_switch]
  S2 = Momentary Switch [package=ksa_sealed_tac_switch]
  R2 = Resistor [tolerance=±5% resistance=220 package=THT]
  R3 = Resistor [tolerance=±5% resistance=220 package=THT]
  7_Segment1 = 7 Segment Display
  R4 = Resistor [tolerance=±5% resistance=220 package=THT]

nets:
  N1: Jetson_Nano2.GND, 7_Segment1.Segment_F, 7_Segment1.Segment_DP, 7_Segment1.Segment_A#10
  N2: Jetson_Nano2.GPIO19, R1.Pin_1, R2.Pin_0, R3.Pin_0, R4.Pin_1
  N3: Jetson_Nano2.GPIO26, S1.2, S2.2
  N4: Jetson_Nano2.ID_SC, S1.4, R2.Pin_1
  N5: Jetson_Nano2.GPIO7, S2.4, R3.Pin_1
  N6: Jetson_Nano2.GPIO24, 7_Segment1.Segment_B
  N7: Jetson_Nano2.GPIO18, 7_Segment1.Segment_C
  N8: Jetson_Nano2.GPIO15, 7_Segment1.Segment_D
  N9: Jetson_Nano2.GPIO14, 7_Segment1.Segment_E
  N10: Jetson_Nano2.5V, 7_Segment1.Segment_A#1
  N11: R1.Pin_0, 7_Segment1.common_cathode#3
  N12: 7_Segment1.common_cathode#8, R4.Pin_0
